# Fritzing sketch Devre şeması (saved by Fritzing 0.9.3b)
breadboards: 1

parts:
  Raspberry_Pi_1 = Raspberry Pi 3 [part_number=RPI-3-V1.2]
  R1 = Resistor [tolerance=±5% resistance=220 package=THT]
  LED1 = LEDs [package=led10mm]

nets:
  N1: Raspberry_Pi_1.GND, LED1.A
  N2: Raspberry_Pi_1.GIPO18, R1.Pin_0
  N3: R1.Pin_1, LED1.C
